// Digital circuit BancoDeRegistradores.dig as structural Verilog
module BancoDeRegistradores (
  input  [7:0] D,
  input  [2:0] Addr_Write,
  input  [2:0] Addr0_Read,
  input  en,
  input  [2:0] Addr1_Read,
  input  Clock,
  output [7:0] Q_0,
  output [7:0] Q_1
);

  wire demultiplexer_1_out_0, demultiplexer_1_out_1, demultiplexer_1_out_2, demultiplexer_1_out_3,
       demultiplexer_1_out_4, demultiplexer_1_out_5, demultiplexer_1_out_6, demultiplexer_1_out_7;
  wire [7:0] register_1_q, register_2_q, register_3_q, register_4_q, register_5_q, register_6_q,
       register_7_q, register_8_q;

  Demultiplexer #(.Selector_Bits(3)) demultiplexer_1 (
    .sel(Addr_Write), .in(en), .out_0(demultiplexer_1_out_0), .out_1(demultiplexer_1_out_1),
    .out_2(demultiplexer_1_out_2), .out_3(demultiplexer_1_out_3), .out_4(demultiplexer_1_out_4),
    .out_5(demultiplexer_1_out_5), .out_6(demultiplexer_1_out_6), .out_7(demultiplexer_1_out_7));
  Register #(.Bits(8)) register_1 (.D(D), .C(Clock), .en(demultiplexer_1_out_0), .Q(register_1_q));
  Register #(.Bits(8)) register_2 (.D(D), .C(Clock), .en(demultiplexer_1_out_1), .Q(register_2_q));
  Register #(.Bits(8)) register_3 (.D(D), .C(Clock), .en(demultiplexer_1_out_2), .Q(register_3_q));
  Register #(.Bits(8)) register_4 (.D(D), .C(Clock), .en(demultiplexer_1_out_3), .Q(register_4_q));
  Register #(.Bits(8)) register_5 (.D(D), .C(Clock), .en(demultiplexer_1_out_4), .Q(register_5_q));
  Register #(.Bits(8)) register_6 (.D(D), .C(Clock), .en(demultiplexer_1_out_5), .Q(register_6_q));
  Register #(.Bits(8)) register_7 (.D(D), .C(Clock), .en(demultiplexer_1_out_6), .Q(register_7_q));
  Register #(.Bits(8)) register_8 (.D(D), .C(Clock), .en(demultiplexer_1_out_7), .Q(register_8_q));
  Multiplexer #(.Selector_Bits(3), .Bits(8)) multiplexer_1 (
    .sel(Addr1_Read), .in_0(register_1_q), .in_1(register_2_q), .in_2(register_3_q), .in_3(register_4_q),
    .in_4(register_5_q), .in_5(register_6_q), .in_6(register_7_q), .in_7(register_8_q), .out(Q_1));
  Multiplexer #(.Selector_Bits(3), .Bits(8)) multiplexer_2 (
    .sel(Addr0_Read), .in_0(register_1_q), .in_1(register_2_q), .in_2(register_3_q), .in_3(register_4_q),
    .in_4(register_5_q), .in_5(register_6_q), .in_6(register_7_q), .in_7(register_8_q), .out(Q_0));
endmodule
