// Digital circuit InvesorCondicional.dig as structural Verilog
module InvesorCondicional (
  input  [7:0] A,
  input  Inv,
  output [7:0] O
);

  assign O = A ^ {8{Inv}};  // XOr xor_1, 8 bits wide
endmodule
