// Digital circuit Processador.dig as structural Verilog
module Processador (
  input  clk
);

  wire counter_1_ovf;
  wire [2:0] eeprom_1_d_2;
  wire [7:0] bancoderegistradores_1_q_0, bancoderegistradores_1_q_1, counter_1_out, ula_1_o_2;
  wire [12:0] eeprom_1_d;

  Counter #(.Bits(8)) counter_1 (.en(1'b1), .C(clk), .clr(counter_1_ovf), .out(counter_1_out), .ovf(counter_1_ovf));
  EEPROM #(.AddrBits(8), .Bits(16)) eeprom_1 (
    .A(counter_1_out), .CS(1'b1), .WE(1'b0), .OE(1'b1), .D({eeprom_1_d_2, eeprom_1_d}));
  BancoDeRegistradores bancoderegistradores_1 (
    .D(ula_1_o_2), .Addr_Write(eeprom_1_d[2:0]), .Addr0_Read(eeprom_1_d[5:3]), .en(1'b1),
    .Addr1_Read(eeprom_1_d[8:6]), .Clock(clk), .Q_0(bancoderegistradores_1_q_0),
    .Q_1(bancoderegistradores_1_q_1));
  ULA ula_1 (
    .A(bancoderegistradores_1_q_0), .B(bancoderegistradores_1_q_1), .A_2(eeprom_1_d[9]),
    .B_2(eeprom_1_d[10]), .O(eeprom_1_d[11]), .SumSub(eeprom_1_d[12]), .Op(eeprom_1_d_2), .O_2(ula_1_o_2));  // open: UA_Overflow, UA_Underflow, UA_CarryOut

  // Notes on the sheet:
  //   contents of eeprom_1 (hex, n*v repeats v):
  //   aaaa,1111,123,1233,121,8787,6756,5434,0,0,0,0,0,0,0,0,0,0,0,0,0,0,1111
endmodule
