// Digital circuit Processador2.dig as structural Verilog
module Processador2 (
  input  clk
);

  wire counter_1_ovf;
  wire [2:0] eeprom_1_d_2;
  wire [7:0] counter_1_out, registerfile_1_da, registerfile_1_db, ula_1_o_2;
  wire [12:0] eeprom_1_d;

  Counter #(.Bits(8)) counter_1 (.en(1'b1), .C(clk), .clr(counter_1_ovf), .out(counter_1_out), .ovf(counter_1_ovf));
  EEPROM #(.AddrBits(8), .Bits(16)) eeprom_1 (
    .A(counter_1_out), .CS(1'b1), .WE(1'b0), .OE(1'b1), .D({eeprom_1_d_2, eeprom_1_d}));
  RegisterFile #(.AddrBits(3), .Bits(8)) registerfile_1 (
    .Din(ula_1_o_2), .we(1'b1), .Rw(eeprom_1_d[2:0]), .C(clk), .Ra(eeprom_1_d[5:3]), .Rb(eeprom_1_d[8:6]),
    .Da(registerfile_1_da), .Db(registerfile_1_db));
  ULA ula_1 (
    .A(registerfile_1_da), .B(registerfile_1_db), .A_2(eeprom_1_d[9]), .B_2(eeprom_1_d[10]),
    .O(eeprom_1_d[11]), .SumSub(eeprom_1_d[12]), .Op(eeprom_1_d_2), .O_2(ula_1_o_2));  // open: UA_Overflow, UA_Underflow, UA_CarryOut

  // Notes on the sheet:
  //   contents of eeprom_1 (hex, n*v repeats v):
  //   aaaa,1111,123,1233,121,8787,6756,5434,0,0,0,0,0,0,0,0,0,0,0,0,0,0,1111
endmodule
