// Digital circuit SomadorCompleto.dig as structural Verilog
module SomadorCompleto (
  input  A,
  input  B,
  input  CarryIn,
  output O,
  output CarryOut
);

  wire and_1_out, and_2_out, xor_1_out;

  xor xor_1 (xor_1_out, A, B);
  and and_1 (and_1_out, A, B);
  xor xor_2 (O, xor_1_out, CarryIn);
  and and_2 (and_2_out, xor_1_out, CarryIn);
  or or_1 (CarryOut, and_2_out, and_1_out);
endmodule
