// Digital circuit SomadorCompleto_8bits.dig as structural Verilog
module SomadorCompleto_8bits (
  input  [7:0] A,
  input  CarryIn,
  input  [7:0] B,
  output [7:0] O,
  output CarryOut
);

  wire S1_carryout, somadorcompleto_1_carryout, somadorcompleto_2_carryout, somadorcompleto_3_carryout,
       somadorcompleto_4_carryout, somadorcompleto_5_carryout, somadorcompleto_6_carryout;

  SomadorCompleto somadorcompleto_1 (
    .A(A[0]), .B(B[0]), .CarryIn(CarryIn), .O(O[0]), .CarryOut(somadorcompleto_1_carryout));
  SomadorCompleto S1 (.A(A[1]), .B(B[1]), .CarryIn(somadorcompleto_1_carryout), .O(O[1]), .CarryOut(S1_carryout));
  SomadorCompleto somadorcompleto_2 (
    .A(A[2]), .B(B[2]), .CarryIn(S1_carryout), .O(O[2]), .CarryOut(somadorcompleto_2_carryout));
  SomadorCompleto somadorcompleto_3 (
    .A(A[3]), .B(B[3]), .CarryIn(somadorcompleto_2_carryout), .O(O[3]), .CarryOut(somadorcompleto_3_carryout));
  SomadorCompleto somadorcompleto_4 (
    .A(A[4]), .B(B[4]), .CarryIn(somadorcompleto_3_carryout), .O(O[4]), .CarryOut(somadorcompleto_4_carryout));
  SomadorCompleto somadorcompleto_5 (
    .A(A[5]), .B(B[5]), .CarryIn(somadorcompleto_4_carryout), .O(O[5]), .CarryOut(somadorcompleto_5_carryout));
  SomadorCompleto somadorcompleto_6 (
    .A(A[6]), .B(B[6]), .CarryIn(somadorcompleto_5_carryout), .O(O[6]), .CarryOut(somadorcompleto_6_carryout));
  SomadorCompleto somadorcompleto_7 (
    .A(A[7]), .B(B[7]), .CarryIn(somadorcompleto_6_carryout), .O(O[7]), .CarryOut(CarryOut));
endmodule
