// Digital circuit ULA.dig as structural Verilog
module ULA (
  input  [7:0] A,
  input  [7:0] B,
  input  A_2,
  input  B_2,
  input  O,
  input  SumSub,
  input  [2:0] Op,
  output [7:0] O_2,
  output UA_Overflow,
  output UA_Underflow,
  output UA_CarryOut
);

  wire [7:0] and_1_out, conditionalinversor_1_p3, conditionalinversor_2_p3, multiplexer_1_out, or_1_out,
       unidadearitmetica_1_o, xor_1_out;

  // ConditionalInversor conditionalinversor_1: pin names not known; wires that end beside it: A, A_2, conditionalinversor_1_p3
  // ConditionalInversor conditionalinversor_2: pin names not known; wires that end beside it: B, B_2, conditionalinversor_2_p3
  assign and_1_out = conditionalinversor_1_p3 & conditionalinversor_2_p3;  // And and_1, 8 bits wide
  assign or_1_out = conditionalinversor_1_p3 | conditionalinversor_2_p3;  // Or or_1, 8 bits wide
  assign xor_1_out = conditionalinversor_1_p3 ^ conditionalinversor_2_p3;  // XOr xor_1, 8 bits wide
  UnidadeAritmetica unidadearitmetica_1 (
    .A(conditionalinversor_1_p3), .B(conditionalinversor_2_p3), .SS(SumSub), .O(unidadearitmetica_1_o),
    .Overflow(UA_Overflow), .Underflow(UA_Underflow), .CarryOut(UA_CarryOut));
  Multiplexer #(.Selector_Bits(3), .Bits(8)) multiplexer_1 (
    .sel(Op), .in_0(and_1_out), .in_1(or_1_out), .in_2(xor_1_out), .in_3(unidadearitmetica_1_o),
    .in_4(conditionalinversor_1_p3), .in_5(conditionalinversor_2_p3), .in_6({8{1'b0}}), .in_7(8'h1),
    .out(multiplexer_1_out));
  // ConditionalInversor conditionalinversor_3: pin names not known; wires that end beside it: multiplexer_1_out, O, O_2
endmodule
