// Digital circuit UnidadeAritmetica.dig as structural Verilog
module UnidadeAritmetica (
  input  [7:0] A,
  input  [7:0] B,
  input  SS,
  output [7:0] O,
  output Overflow,
  output Underflow,
  output CarryOut
);

  wire [7:0] conditionalinversor_1_p3;

  // ConditionalInversor conditionalinversor_1: pin names not known; wires that end beside it: B, SS, conditionalinversor_1_p3
  SomadorCompleto_8bits somadorcompleto_8bits_1 (
    .A(A), .CarryIn(SS), .B(conditionalinversor_1_p3), .O(O), .CarryOut(CarryOut));
  and and_1 (Overflow, ~SS, CarryOut);  // And
  and and_2 (Underflow, ~CarryOut, SS);  // And
endmodule
